# Fritzing sketch JaacgPhase1 (saved by Fritzing 0.9.3b)
breadboards: 1

parts:
  Bauteil1 = Arduino Mega 2560 (Rev3)  # not connected
  DHT1 = DHT22 Humidity and Temperature Sensor
  DHT2 = DHT11 Humitidy and Temperature Sensor
  R1 = Resistor [tolerance=±5% resistance=10k package=THT]
  R2 = Resistor [tolerance=±5% resistance=4.7k package=THT]
  DHT3 = DHT22 Humidity and Temperature Sensor
  R3 = Resistor [tolerance=±5% resistance=10k package=THT]

nets:
  VDD: DHT1.VDD, DHT2.VDD, R1.Pin_0, R2.Pin_0, DHT3.VDD, R3.Pin_0
  N1: DHT1.DATA, R1.Pin_1
  GND: DHT1.GND, DHT2.GND, DHT3.GND
  N2: DHT2.DATA, R2.Pin_1
  N3: DHT3.DATA, R3.Pin_1

notes:
  Grün: GND
  Rot: 3,3V
  Gelb 5V
  Datenkabel: Blau

custom parts:
  DHT11 Humitidy and Temperature Sensor: DHT11 Humidity and Temperature Sensor
